# Fritzing sketch KvizzyVid17flat (saved by Fritzing 1.0.2b)
breadboards: 1

parts:
  ESP32-C3_SuperMini1 = ESP32-C3_SuperMini
  R1 = Resistor [tolerance=±5% power=0.25W resistance=1M package=THT]
  R2 = Resistor [tolerance=±5% power=0.25W resistance=1M package=THT]
  Компонент1 = NRF24L01+ Breakout Board

nets:
  N1: ESP32-C3_SuperMini1.connector0, R1.Pin_0
  N2: ESP32-C3_SuperMini1.connector4, Компонент1.SCK
  N3: ESP32-C3_SuperMini1.connector5, Компонент1.MISO
  N4: ESP32-C3_SuperMini1.connector6, Компонент1.MOSI
  N5: ESP32-C3_SuperMini1.connector7, Компонент1.CS
  N6: ESP32-C3_SuperMini1.connector10, Компонент1.CE
  N7: ESP32-C3_SuperMini1.connector97, R2.Pin_1, Компонент1.VCC
  N8: ESP32-C3_SuperMini1.connector98, R1.Pin_1, Компонент1.GND
