# Fritzing sketch NANO-nRF24L01 (saved by Fritzing 1.0.2b)
breadboards: 1

parts:
  Компонент1 = Arduino Nano (Rev3.0) (ICSP)
  nRF24L01_PA1 = nRF24L01 power adapter [package="DIP (Dual Inline) [THT]"]
  Компонент2 = NRF24L01+ Breakout Board  # not connected

nets:
  GND: Компонент1.GND, nRF24L01_PA1.GND
  N1: Компонент1.D6, nRF24L01_PA1.CE
  N2: Компонент1.D7, nRF24L01_PA1.CSN
  N3: Компонент1.D11/MOSI, nRF24L01_PA1.MO
  N4: Компонент1.D12/MISO, nRF24L01_PA1.MI
  5V: Компонент1.5V, nRF24L01_PA1.VCC
  N5: Компонент1.D13/SCK, nRF24L01_PA1.SCK

custom parts:
  nRF24L01 power adapter: Адаптер для питания nRF
