# Fritzing sketch UNO-nRF24L01 (saved by Fritzing 1.0.2b)

parts:
  nRF24L01_PA1 = nRF24L01 power adapter [package="DIP (Dual Inline) [THT]"]
  Компонент2 = NRF24L01+ Breakout Board  # not connected
  Компонент3 = Arduino Uno (Rev3) - ICSP

nets:
  GND: nRF24L01_PA1.GND, Компонент3.GND
  VCC: nRF24L01_PA1.VCC, Компонент3.5V
  N1: nRF24L01_PA1.CE, Компонент3.D6_PWM
  N2: nRF24L01_PA1.CSN, Компонент3.D7
  N3: nRF24L01_PA1.SCK, Компонент3.ICSP_SCK, Компонент3.D13/SCK
  N4: nRF24L01_PA1.MO, Компонент3.ICSP_MOSI, Компонент3.D11_PWM/MOSI
  N5: nRF24L01_PA1.MI, Компонент3.ICSP_MISO, Компонент3.D12/MISO

custom parts:
  nRF24L01 power adapter: Адаптер для питания nRF
